# Fritzing sketch FanTester (saved by Fritzing 0.9.3b)
circuit board: 7.62cm x 5.08cm
breadboards: 2

parts:
  Arduino_Nano = Arduino Nano (Rev3.0)
  BATT = Battery block 9V
  R2 = Resistor [tolerance=±5% resistance=3.3k package=THT]
  R3 = Resistor [tolerance=±1% resistance=5.6 package=THT]
  Q1 = MOSFET-NCHANNEL [package=to220v]
  Q2 = MOSFET-NCHANNEL [package=to-92]
  R4 = Resistor [tolerance=±1% resistance=5.6 package=THT]
  R5 = Resistor [tolerance=±1% resistance=5.6 package=THT]
  R6 = Resistor [tolerance=±1% resistance=5.6 package=THT]
  R7 = Resistor [tolerance=±1% resistance=5.6 package=THT]
  C1 = Capacitor Polarized [part_number=10uF package=cpol-radial-100uf-25v]
  S1 = SPST Switch [package=switch-spdt]
  S2 = SPST Switch [package=switch-spdt]
  R8 = Resistor [tolerance=±1% resistance=82k package=THT]
  R9 = Resistor [tolerance=±1% resistance=100k package=THT]
  R1 = Resistor [tolerance=±1% resistance=100k package=THT]
  EXT = Battery block 9V
  R10 = Resistor [tolerance=±1% resistance=120 power=1W package=THT]
  RS232 = Header 4 [package=molex-1x4_lock]
  ROTARY = Header 6 [package=molex-1x6_lock]
  R12 = Resistor [tolerance=±1% resistance=100k package=THT]
  R13 = Resistor [tolerance=±1% resistance=140k package=THT]
  FAN_/_LEDS = Header 6 [package=molex-1x6_lock]
  C2 = Capacitor [part_number=0.47uF package=cap-pth-5mm]
  C3 = Capacitor [part_number=0.47uF package=cap-pth-5mm]
  C4 = Capacitor [part_number=0.1uF package=cap-pth-small2]
  C5 = Capacitor [part_number=0.1uF package=cap-pth-small2]
  D1 = Diode [package=diode-1n4001]
  Display = Header 4 [package=molex-1x4_lock]
  R11 = Resistor [tolerance=±1% resistance=100k package=THT]

nets:
  GND: Arduino_Nano.GND, BATT.-, R3.Pin_1, Q2.S, R4.Pin_0, R5.Pin_0, R6.Pin_0, R7.Pin_0, C1.-, R9.Pin_1, R1.Pin_0, EXT.-, RS232.4, ROTARY.2, R12.Pin_0, C2.1, C3.1, C4.1, C5.1, Display.1, R11.Pin_0
  CLK: Arduino_Nano.D2, ROTARY.3, C3.2
  N1: Arduino_Nano.D3, FAN_/_LEDS.3
  N2: Arduino_Nano.D4, Q2.G, R1.Pin_1
  N3: Arduino_Nano.D5, FAN_/_LEDS.4
  N4: Arduino_Nano.D6, RS232.1
  N5: Arduino_Nano.D7, RS232.2
  SW: Arduino_Nano.D10, ROTARY.5
  DT: Arduino_Nano.D11/MOSI, ROTARY.4
  N6: Arduino_Nano.D12/MISO, Q1.G, R11.Pin_1
  9V: Arduino_Nano.VIN, C1.+, S1.P, S2.O, R8.Pin_0, FAN_/_LEDS.6
  5V: Arduino_Nano.5V, RS232.3, ROTARY.1, C4.2, C5.2, Display.2
  N7: Arduino_Nano.A5, Display.4
  N8: Arduino_Nano.A4, Display.3
  N9: Arduino_Nano.A2, R2.Pin_0, C2.2
  N10: Arduino_Nano.A1, R8.Pin_1, R9.Pin_0
  12VMON: Arduino_Nano.A0, R12.Pin_1, R13.Pin_0
  N11: BATT.+, S1.S
  N12: R2.Pin_1, R3.Pin_0, Q1.S, R4.Pin_1, R5.Pin_1, R6.Pin_1, R7.Pin_1
  N13: Q1.D, FAN_/_LEDS.1, D1.A
  N14: Q2.D, R10.Pin_0
  N15: S2.P, R13.Pin_1, FAN_/_LEDS.2, D1.C
  N16: S2.S, EXT.+
  N17: R10.Pin_1, FAN_/_LEDS.5

notes:
  2017 - Bill Williams
  Fan Tester
  5V
  GND
  CLK
  DT
  SW
  RTN
  PWR
  TACH
  PWM
  TX
  RX
  LED-
  BAT
  Fan Tester, Arduino Controlled Fan Tester, -
  SDA
  SCL
